// Logisim project letra A Atividade 4.circ as structural Verilog: 1 circuit, main circuit main
module main (
  input  A,
  input  B,
  input  C,
  input  A_2,
  input  B_2,
  input  C_2,
  output X,
  output X_2
);

  wire and_1_out, not_1_out, not_2_out, not_3_out;

  not not_1 (not_1_out, A);
  not not_2 (not_2_out, C);
  not not_3 (not_3_out, B_2);
  or or_1 (X_2, A_2, not_3_out, C_2);
  not not_4 (X, and_1_out);
  and and_1 (and_1_out, not_1_out, B, not_2_out);

  // Notes on the sheet:
  //   DeMorgan
endmodule
