// Logisim project letra B Atividade 4.circ as structural Verilog: 1 circuit, main circuit main
module main (
  input  A,
  input  B,
  input  C,
  input  A_2,
  input  B_2,
  input  C_2,
  output X,
  output X_2
);

  wire and_1_out, and_2_out, not_1_out, not_2_out, not_3_out, or_1_out;

  not not_1 (not_1_out, B);
  not not_2 (not_2_out, A);
  and and_1 (and_1_out, not_1_out, C);
  and and_2 (and_2_out, A_2, B_2);
  not not_3 (not_3_out, C_2);
  or or_1 (or_1_out, not_2_out, and_1_out);
  not not_4 (X, or_1_out);
  or or_2 (X_2, and_2_out, not_3_out);

  // Notes on the sheet:
  //   DeMorgan
endmodule
