// Logisim project letra C Atividade 4.circ as structural Verilog: 1 circuit, main circuit main
module main (
  input  A,
  input  B,
  input  C,
  input  D,
  input  A_2,
  input  B_2,
  input  C_2,
  input  D_2,
  output X,
  output DeMorgan
);

  wire and_1_out, and_2_out, not_1_out, not_2_out, not_3_out, not_4_out;

  not not_1 (not_1_out, C);
  not not_2 (not_2_out, D);
  not not_3 (not_3_out, A_2);
  not not_4 (not_4_out, B_2);
  and and_1 (and_1_out, C_2, D_2);
  and and_2 (and_2_out, A, B, not_1_out, not_2_out);
  not not_5 (X, and_2_out);
  or or_1 (DeMorgan, not_3_out, not_4_out, and_1_out);
endmodule
