// Logisim project letra D  Atividade 4.circ as structural Verilog: 1 circuit, main circuit main
module main (
  input  A,
  input  B,
  input  A_2,
  input  B_2,
  output X,
  output X_2
);

  wire not_1_out, not_2_out, or_1_out;

  not not_1 (not_1_out, B);
  not not_2 (not_2_out, A_2);
  or or_1 (or_1_out, A, not_1_out);
  and and_1 (X_2, not_2_out, B_2);
  not not_3 (X, or_1_out);

  // Notes on the sheet:
  //   DeMorgan
endmodule
