// Logisim project letra E  Atividade 4.circ as structural Verilog: 1 circuit, main circuit main
module main (
  input  A,
  input  B,
  input  A_2,
  input  B_2,
  output X,
  output X_2
);

  wire and_1_out, not_1_out;

  and and_1 (and_1_out, A, B);
  and and_2 (X_2, A_2, B_2);
  not not_1 (not_1_out, and_1_out);
  not not_2 (X, not_1_out);

  // Notes on the sheet:
  //   DeMorgan
endmodule
