// Logisim project letra F  Atividade 4.circ as structural Verilog: 1 circuit, main circuit main
module main (
  input  A,
  input  C,
  input  D,
  input  A_2,
  input  C_2,
  input  D_2,
  output X,
  output X_2
);

  wire not_1_out, not_2_out, not_3_out, or_1_out;

  not not_1 (not_1_out, A);
  not not_2 (not_2_out, C);
  not not_3 (not_3_out, D);
  or or_1 (or_1_out, not_1_out, not_2_out, not_3_out);
  not not_4 (X, or_1_out);
  and and_1 (X_2, A_2, C_2, D_2);

  // Notes on the sheet:
  //   DeMorgan
endmodule
