// Logisim project letra G  Atividade 4.circ as structural Verilog: 1 circuit, main circuit main
module main (
  input  A,
  input  B,
  input  C,
  input  D,
  input  A_2,
  input  B_2,
  input  C_2,
  input  D_2,
  output X,
  output X_2
);

  wire and_1_out, not_1_out, not_2_out, not_3_out, not_4_out, not_5_out, or_1_out, or_2_out;

  not not_1 (not_1_out, C);
  not not_2 (not_2_out, C_2);
  or or_1 (or_1_out, B, not_1_out);
  not not_3 (not_3_out, or_1_out);
  not not_4 (not_4_out, A_2);
  or or_2 (or_2_out, B_2, not_2_out);
  not not_5 (not_5_out, D_2);
  and and_1 (and_1_out, A, not_3_out, D);
  not not_6 (X, and_1_out);
  or or_3 (X_2, not_4_out, or_2_out, not_5_out);

  // Notes on the sheet:
  //   DeMorgan
endmodule
