// Logisim project letra H  Atividade 4.circ as structural Verilog: 1 circuit, main circuit main
module main (
  input  M,
  input  N,
  input  M_2,
  input  N_2,
  input  M_3,
  input  N_3,
  input  M_4,
  input  N_4,
  output out_9,
  output x
);

  wire and_1_out, and_2_out, and_3_out, not_1_out, not_2_out, not_3_out, not_4_out, or_1_out, or_2_out;

  not not_1 (not_1_out, M);
  not not_2 (not_2_out, N_2);
  not not_3 (not_3_out, M_3);
  not not_4 (not_4_out, N_4);
  or or_1 (or_1_out, not_1_out, N);
  or or_2 (or_2_out, M_2, not_2_out);
  and and_1 (and_1_out, not_3_out, N_3);
  and and_2 (and_2_out, M_4, not_4_out);
  and and_3 (and_3_out, or_1_out, or_2_out);
  not not_5 (out_9, and_3_out);
  or or_3 (x, and_1_out, and_2_out);

  // Notes on the sheet:
  //   DeMorgan
endmodule
