// Logisim project letra I  Atividade 4.circ as structural Verilog: 1 circuit, main circuit main
module main (
  input  A,
  input  B,
  input  C,
  input  D,
  input  A_2,
  input  B_2,
  input  C_2,
  input  D_2,
  output X,
  output X_2
);

  wire and_1_out, not_1_out, not_2_out, not_3_out, not_4_out, or_1_out, or_2_out, or_3_out, or_5_out;

  or or_1 (or_1_out, A, B);
  or or_2 (or_2_out, A_2, B_2);
  not not_1 (not_1_out, or_1_out);
  not not_2 (not_2_out, or_2_out);
  and and_1 (and_1_out, not_2_out, C_2);
  or or_3 (or_3_out, not_1_out, C);
  not not_3 (not_3_out, D_2);
  not not_4 (not_4_out, or_3_out);
  or or_4 (X_2, and_1_out, not_3_out);
  or or_5 (or_5_out, not_4_out, D);
  not not_5 (X, or_5_out);

  // Notes on the sheet:
  //   DeMorgan
endmodule
