// Logisim project Atividade 2 CD Gian.circ as structural Verilog: 7 circuits, main circuit Atividade 3
// A
module Atividade_3 (
  input  A,
  input  B,
  input  A_2,
  input  B_2,
  input  C,
  input  C_2,
  input  D,
  input  A_3,
  input  B_3,
  input  C_3,
  input  D_2,
  output Z,
  output X,
  output Y
);

  wire and_1_out, and_2_out, and_3_out, and_4_out, and_5_out, and_6_out, and_7_out, and_8_out, and_9_out,
       not_1_out, not_2_out, not_3_out, not_4_out, not_5_out, not_6_out, not_7_out, not_8_out, not_9_out,
       not_10_out, not_11_out, not_12_out, not_13_out, not_14_out, not_15_out;

  not not_1 (not_1_out, A);
  not not_2 (not_2_out, B);
  not not_3 (not_3_out, A);
  not not_4 (not_4_out, C);
  not not_5 (not_5_out, D);
  and and_1 (and_1_out, not_1_out, not_2_out);
  and and_2 (and_2_out, not_3_out, B, not_4_out);
  and and_3 (and_3_out, A, C, not_5_out);
  not not_6 (not_6_out, A_3);
  not not_7 (not_7_out, B_3);
  not not_8 (not_8_out, C_3);
  not not_9 (not_9_out, B_3);
  not not_10 (not_10_out, A_3);
  not not_11 (not_11_out, D_2);
  not not_12 (not_12_out, B_3);
  not not_13 (not_13_out, D_2);
  and and_4 (and_4_out, not_6_out, not_7_out, not_8_out);
  and and_5 (and_5_out, not_9_out, C_3, D_2);
  and and_6 (and_6_out, not_10_out, C_3, not_11_out);
  and and_7 (and_7_out, A_3, not_12_out, not_13_out);
  or or_1 (X, and_1_out, and_2_out, and_3_out);
  or or_2 (Y, and_4_out, and_5_out, and_6_out, and_7_out);
  not not_14 (not_14_out, C_2);
  and and_8 (and_8_out, A_2, B_2);
  and and_9 (and_9_out, A_2, not_14_out);
  not not_15 (not_15_out, and_8_out);
  or or_3 (Z, not_15_out, and_9_out);

  // Notes on the sheet:
  //   A)
  //   B)
  //   Atividade 3
  //   C)
endmodule

module AT_2_a (
  input  A,
  input  C,
  input  B,
  output X
);

  wire and_1_out, and_2_out, not_1_out;

  not not_1 (not_1_out, A);
  and and_1 (and_1_out, not_1_out, C);
  and and_2 (and_2_out, B, C);
  or or_1 (X, and_1_out, and_2_out);
endmodule

module AT_2_b (
  input  Q,
  input  R,
  output Y
);

  wire and_1_out, and_2_out, not_1_out, not_2_out;

  not not_1 (not_1_out, R);
  not not_2 (not_2_out, Q);
  and and_1 (and_1_out, Q, not_1_out);
  and and_2 (and_2_out, not_2_out, R);
  or or_1 (Y, and_1_out, and_2_out);
endmodule

module AT_2_C (
  input  C,
  input  A,
  output W
);

  wire not_1_out;

  not not_1 (not_1_out, A);
  or or_1 (W, C, not_1_out);
endmodule

module AT_2_D (
  input  A,
  input  B,
  input  C,
  output X
);

  wire and_1_out, and_2_out, and_3_out, not_1_out, not_2_out, not_3_out;

  not not_1 (not_1_out, B);
  not not_2 (not_2_out, C);
  not not_3 (not_3_out, B);
  and and_1 (and_1_out, not_1_out, not_2_out);
  and and_2 (and_2_out, B, C);
  and and_3 (and_3_out, A, not_3_out);
  or or_1 (X, and_1_out, and_2_out, and_3_out);
endmodule

module AT_2_E (
  input  A,
  input  B,
  input  C,
  input  D,
  output Y
);

  wire and_1_out, not_1_out, not_2_out, not_3_out, not_4_out;

  not not_1 (not_1_out, A);
  not not_2 (not_2_out, B);
  and and_1 (and_1_out, not_1_out, not_2_out);
  not not_3 (not_3_out, C);
  not not_4 (not_4_out, D);
  or or_1 (Y, and_1_out, not_3_out, not_4_out);
endmodule

module AT_2_F (
  input  A,
  input  B,
  input  C,
  input  D,
  output X
);

  wire and_1_out, and_2_out, and_3_out, and_4_out, not_1_out, not_2_out, not_3_out, not_4_out, not_5_out,
       not_6_out, not_7_out, not_8_out;

  not not_1 (not_1_out, A);
  not not_2 (not_2_out, B);
  not not_3 (not_3_out, C);
  not not_4 (not_4_out, D);
  not not_5 (not_5_out, C);
  not not_6 (not_6_out, D);
  not not_7 (not_7_out, A);
  not not_8 (not_8_out, D);
  and and_1 (and_1_out, not_1_out, not_2_out, not_3_out, not_4_out);
  and and_2 (and_2_out, A, not_5_out, not_6_out);
  and and_3 (and_3_out, B, not_7_out, not_8_out);
  and and_4 (and_4_out, A, B, C);
  or or_1 (X, and_1_out, and_2_out, and_3_out, and_4_out);
endmodule
